// Logisim project Digital Clock 2107005.circ as structural Verilog: 17 circuits, main circuit main
module main (
  input  Load,
  input  Hour,
  input  [3:0] in_3,
  input  [2:0] Minute,
  input  [3:0] in_5,
  input  [2:0] Second,
  input  [3:0] Minute_2,
  input  in_8
);

  wire bcd_to_binary_1_lsb, bcd_to_binary_1_msb, bcd_to_binary_1_out_7, bcd_to_binary_1_out_8,
       bcdto7_1_out_5, bcdto7_1_out_6, bcdto7_1_out_7, bcdto7_1_out_8, bcdto7_1_out_9, bcdto7_1_out_10,
       bcdto7_1_out_11, bcdto7_2_out_5, bcdto7_2_out_7, bcdto7_2_out_8, bcdto7_2_out_9, bcdto7_2_out_10,
       bcdto7_2_out_11, bcdto7_3_out_5, bcdto7_3_out_6, bcdto7_3_out_7, bcdto7_3_out_8, bcdto7_3_out_9,
       bcdto7_3_out_10, bcdto7_3_out_11, bcdto7_4_out_5, bcdto7_4_out_6, bcdto7_4_out_7, bcdto7_4_out_8,
       bcdto7_4_out_9, bcdto7_4_out_10, bcdto7_4_out_11, bcdto7_5_out_5, bcdto7_5_out_6, bcdto7_5_out_7,
       bcdto7_5_out_8, bcdto7_5_out_9, bcdto7_5_out_10, bcdto7_5_out_11, bcdto7_6_out_5, bcdto7_6_out_6,
       bcdto7_6_out_7, bcdto7_6_out_8, bcdto7_6_out_9, bcdto7_6_out_10, bcdto7_6_out_11,
       binary_to_bcd_1_lsb_2, binary_to_bcd_1_msb_2, binary_to_bcd_1_out_6, binary_to_bcd_1_out_7,
       binary_to_bcd_1_out_8, Clk_out, mod_13_counter_1_lsb_2, mod_13_counter_1_msb_2,
       mod_13_counter_1_out_9, mod_13_counter_1_out_10, mod_60_counter_1_lsb_2, mod_60_counter_1_msb_2,
       mod_60_counter_1_out_12, mod_60_counter_1_out_13, mod_60_counter_1_out_14, mod_60_counter_1_out_15,
       mod_60_counter_1_out_16, mod_60_counter_2_lsb_2, mod_60_counter_2_msb_2, mod_60_counter_2_out_12,
       mod_60_counter_2_out_13, mod_60_counter_2_out_14, mod_60_counter_2_out_15, mod_60_counter_2_out_16,
       or_1_out, or_2_out;

  Clock Clk (.out(Clk_out));
  BCD_to_Binary bcd_to_binary_1 (
    .C4(Hour), .C3(in_3[3]), .C2(in_3[2]), .C1(in_3[1]), .C0(in_3[0]), .MSB(bcd_to_binary_1_msb),
    .out_7(bcd_to_binary_1_out_7), .out_8(bcd_to_binary_1_out_8), .LSB(bcd_to_binary_1_lsb));
  bcdto7 bcdto7_1 (
    .in_1(1'b0), .in_2(1'b0), .in_3(1'b0), .in_4(binary_to_bcd_1_msb_2), .out_5(bcdto7_1_out_5),
    .out_6(bcdto7_1_out_6), .out_7(bcdto7_1_out_7), .out_8(bcdto7_1_out_8), .out_9(bcdto7_1_out_9),
    .out_10(bcdto7_1_out_10), .out_11(bcdto7_1_out_11));
  Binary_to_BCD binary_to_bcd_1 (
    .MSB_2(binary_to_bcd_1_msb_2), .out_6(binary_to_bcd_1_out_6), .out_7(binary_to_bcd_1_out_7),
    .out_8(binary_to_bcd_1_out_8), .LSB_2(binary_to_bcd_1_lsb_2), .MSB(mod_13_counter_1_msb_2),
    .in_2(mod_13_counter_1_out_9), .in_3(mod_13_counter_1_out_10), .LSB(mod_13_counter_1_lsb_2));
  Mod_13_Counter mod_13_counter_1 (
    .Clk(or_1_out), .Decision_for_Load(Load), .MSB(bcd_to_binary_1_msb), .in_4(bcd_to_binary_1_out_7),
    .in_5(bcd_to_binary_1_out_8), .LSB(bcd_to_binary_1_lsb), .MSB_2(mod_13_counter_1_msb_2),
    .out_9(mod_13_counter_1_out_9), .out_10(mod_13_counter_1_out_10), .LSB_2(mod_13_counter_1_lsb_2),
    .Enable(in_8));
  _7_Segment_Display u_7_segment_display_1 (
    .g(bcdto7_1_out_11), .f(bcdto7_1_out_10), .a(bcdto7_1_out_5), .b(bcdto7_1_out_6), .e(bcdto7_1_out_9),
    .d(bcdto7_1_out_8), .c(bcdto7_1_out_7));  // open: dp
  bcdto7 bcdto7_2 (
    .in_1(binary_to_bcd_1_out_6), .in_2(binary_to_bcd_1_out_7), .in_3(binary_to_bcd_1_out_8),
    .in_4(binary_to_bcd_1_lsb_2), .out_5(bcdto7_2_out_5), .out_6(bcdto7_2_out_5), .out_7(bcdto7_2_out_7),
    .out_8(bcdto7_2_out_8), .out_9(bcdto7_2_out_9), .out_10(bcdto7_2_out_10), .out_11(bcdto7_2_out_11));
  or or_1 (or_1_out, mod_60_counter_1_msb_2, mod_60_counter_1_out_12, mod_60_counter_1_out_13);
  _7_Segment_Display u_7_segment_display_2 (
    .g(bcdto7_2_out_11), .f(bcdto7_2_out_10), .a(bcdto7_2_out_5), .b(bcdto7_2_out_5), .e(bcdto7_2_out_9),
    .d(bcdto7_2_out_8), .c(bcdto7_2_out_7));  // open: dp
  bcdto7 bcdto7_3 (
    .in_1(1'b0), .in_2(mod_60_counter_1_msb_2), .in_3(mod_60_counter_1_out_12),
    .in_4(mod_60_counter_1_out_13), .out_5(bcdto7_3_out_5), .out_6(bcdto7_3_out_6), .out_7(bcdto7_3_out_7),
    .out_8(bcdto7_3_out_8), .out_9(bcdto7_3_out_9), .out_10(bcdto7_3_out_10), .out_11(bcdto7_3_out_11));
  _7_Segment_Display u_7_segment_display_3 (
    .g(bcdto7_3_out_11), .f(bcdto7_3_out_10), .a(bcdto7_3_out_5), .b(bcdto7_3_out_6), .e(bcdto7_3_out_9),
    .d(bcdto7_3_out_8), .c(bcdto7_3_out_7));  // open: dp
  bcdto7 bcdto7_4 (
    .in_1(mod_60_counter_1_out_14), .in_2(mod_60_counter_1_out_15), .in_3(mod_60_counter_1_out_16),
    .in_4(mod_60_counter_1_lsb_2), .out_5(bcdto7_4_out_5), .out_6(bcdto7_4_out_6), .out_7(bcdto7_4_out_7),
    .out_8(bcdto7_4_out_8), .out_9(bcdto7_4_out_9), .out_10(bcdto7_4_out_10), .out_11(bcdto7_4_out_11));
  Mod_60_counter mod_60_counter_1 (
    .CLk(or_2_out), .Decision_for_load(Load), .MSB(Minute[2]), .in_4(Minute[1]), .in_5(Minute[0]),
    .in_6(in_5[3]), .in_7(in_5[2]), .in_8(in_5[1]), .LSB(in_5[0]), .Enable(in_8),
    .MSB_2(mod_60_counter_1_msb_2), .out_12(mod_60_counter_1_out_12), .out_13(mod_60_counter_1_out_13),
    .out_14(mod_60_counter_1_out_14), .out_15(mod_60_counter_1_out_15), .out_16(mod_60_counter_1_out_16),
    .LSB_2(mod_60_counter_1_lsb_2));
  _7_Segment_Display u_7_segment_display_4 (
    .g(bcdto7_4_out_11), .f(bcdto7_4_out_10), .a(bcdto7_4_out_5), .b(bcdto7_4_out_6), .e(bcdto7_4_out_9),
    .d(bcdto7_4_out_8), .c(bcdto7_4_out_7));  // open: dp
  bcdto7 bcdto7_5 (
    .in_1(1'b0), .in_2(mod_60_counter_2_msb_2), .in_3(mod_60_counter_2_out_12),
    .in_4(mod_60_counter_2_out_13), .out_5(bcdto7_5_out_5), .out_6(bcdto7_5_out_6), .out_7(bcdto7_5_out_7),
    .out_8(bcdto7_5_out_8), .out_9(bcdto7_5_out_9), .out_10(bcdto7_5_out_10), .out_11(bcdto7_5_out_11));
  _7_Segment_Display u_7_segment_display_5 (
    .g(bcdto7_5_out_11), .f(bcdto7_5_out_10), .a(bcdto7_5_out_5), .b(bcdto7_5_out_6), .e(bcdto7_5_out_9),
    .d(bcdto7_5_out_8), .c(bcdto7_5_out_7));  // open: dp
  or or_2 (or_2_out, mod_60_counter_2_msb_2, mod_60_counter_2_out_12, mod_60_counter_2_out_13);
  bcdto7 bcdto7_6 (
    .in_1(mod_60_counter_2_out_14), .in_2(mod_60_counter_2_out_15), .in_3(mod_60_counter_2_out_16),
    .in_4(mod_60_counter_2_lsb_2), .out_5(bcdto7_6_out_5), .out_6(bcdto7_6_out_6), .out_7(bcdto7_6_out_7),
    .out_8(bcdto7_6_out_8), .out_9(bcdto7_6_out_9), .out_10(bcdto7_6_out_10), .out_11(bcdto7_6_out_11));
  Mod_60_counter mod_60_counter_2 (
    .CLk(Clk_out), .Decision_for_load(Load), .MSB(Second[2]), .in_4(Second[1]), .in_5(Second[0]),
    .in_6(Minute_2[3]), .in_7(Minute_2[2]), .in_8(Minute_2[1]), .LSB(Minute_2[0]), .Enable(in_8),
    .MSB_2(mod_60_counter_2_msb_2), .out_12(mod_60_counter_2_out_12), .out_13(mod_60_counter_2_out_13),
    .out_14(mod_60_counter_2_out_14), .out_15(mod_60_counter_2_out_15), .out_16(mod_60_counter_2_out_16),
    .LSB_2(mod_60_counter_2_lsb_2));
  _7_Segment_Display u_7_segment_display_6 (
    .g(bcdto7_6_out_11), .f(bcdto7_6_out_10), .a(bcdto7_6_out_5), .b(bcdto7_6_out_6), .e(bcdto7_6_out_9),
    .d(bcdto7_6_out_8), .c(bcdto7_6_out_7));  // open: dp

  // Notes on the sheet:
  //   2107005
endmodule

module Decision (
  input  D,
  input  X,
  input  Y,
  output out_4
);

  wire and_1_out, and_2_out, not_1_out;

  not not_1 (not_1_out, D);
  and and_1 (and_1_out, D, X);
  and and_2 (and_2_out, not_1_out, Y);
  or or_1 (out_4, and_1_out, and_2_out);

  // Notes on the sheet:
  //   2107005
endmodule

module Mod_6_Counter (
  input  Clk,
  input  Decision,
  input  MSB,
  input  Enable,
  input  in_5,
  input  LSB,
  output Qa,
  output Qb,
  output Qc
);

  wire and_1_out, and_2_out, load_identifier_1_clear, load_identifier_1_preset, load_identifier_2_clear,
       load_identifier_2_preset, load_identifier_3_clear, load_identifier_3_preset, or_1_out, t_ff_3_qn;

  Load_Identifier load_identifier_1 (
    .Decision(Decision), .Load(MSB), .Preset(load_identifier_1_preset), .Clear(load_identifier_1_clear));
  Load_Identifier load_identifier_2 (
    .Decision(Decision), .Load(in_5), .Preset(load_identifier_2_preset), .Clear(load_identifier_2_clear));
  Load_Identifier load_identifier_3 (
    .Decision(Decision), .Load(LSB), .Preset(load_identifier_3_preset), .Clear(load_identifier_3_clear));
  T_Flip_Flop #(.trigger("falling")) t_ff_1 (
    .clk(Clk), .T(1'b1), .Q(Qc), .preset(load_identifier_3_preset), .reset(load_identifier_3_clear),
    .en(Enable));  // open: Qn
  T_Flip_Flop #(.trigger("falling")) t_ff_2 (
    .clk(Clk), .T(and_1_out), .Q(Qb), .preset(load_identifier_2_preset), .reset(load_identifier_2_clear),
    .en(Enable));  // open: Qn
  and and_1 (and_1_out, Qc, t_ff_3_qn);
  and and_2 (and_2_out, Qc, or_1_out);
  T_Flip_Flop #(.trigger("falling")) t_ff_3 (
    .clk(Clk), .T(and_2_out), .Q(Qa), .Qn(t_ff_3_qn), .preset(load_identifier_1_preset),
    .reset(load_identifier_1_clear), .en(Enable));
  or or_1 (or_1_out, Qb, Qa);

  // Notes on the sheet:
  //   2107005
endmodule

module BCD_Counter (
  input  Clk,
  input  Decision_for_load,
  input  MSB,
  input  in_4,
  input  in_5,
  input  LSB,
  input  Decision_for_Skip,
  input  Enable,
  output Qa,
  output Qb,
  output Qc,
  output Qd
);

  wire and_1_out, and_2_out, and_3_out, and_4_out, decision_1_out_4, decision_2_out_4, decision_3_out_4,
       decision_4_out_4, j_k_ff_3_qn, j_k_ff_4_qn, load_identifier_1_clear, load_identifier_1_preset,
       load_identifier_2_clear, load_identifier_2_preset, load_identifier_3_clear, load_identifier_3_preset,
       load_identifier_4_clear, load_identifier_4_preset, or_1_out, or_2_out;

  Load_Identifier load_identifier_1 (
    .Decision(Decision_for_load), .Load(MSB), .Preset(load_identifier_1_preset),
    .Clear(load_identifier_1_clear));
  Load_Identifier load_identifier_2 (
    .Decision(Decision_for_load), .Load(in_4), .Preset(load_identifier_2_preset),
    .Clear(load_identifier_2_clear));
  Load_Identifier load_identifier_3 (
    .Decision(Decision_for_load), .Load(in_5), .Preset(load_identifier_3_preset),
    .Clear(load_identifier_3_clear));
  Load_Identifier load_identifier_4 (
    .Decision(Decision_for_load), .Load(LSB), .Preset(load_identifier_4_preset),
    .Clear(load_identifier_4_clear));
  J_K_Flip_Flop #(.trigger("falling")) j_k_ff_1 (
    .J(decision_1_out_4), .clk(Clk), .K(1'b1), .Q(Qd), .preset(load_identifier_4_preset), .en(Enable),
    .reset(load_identifier_4_clear));  // open: Qn
  Decision decision_1 (.D(Decision_for_Skip), .X(or_1_out), .Y(1'b1), .out_4(decision_1_out_4));
  J_K_Flip_Flop #(.trigger("falling")) j_k_ff_2 (
    .J(decision_3_out_4), .clk(Clk), .K(Qd), .Q(Qc), .preset(load_identifier_3_preset), .en(Enable),
    .reset(load_identifier_3_clear));  // open: Qn
  or or_1 (or_1_out, Qc, j_k_ff_3_qn);
  Decision decision_2 (.D(Decision_for_Skip), .X(Qd), .Y(and_1_out), .out_4(decision_2_out_4));
  and and_1 (and_1_out, Qc, Qd);
  J_K_Flip_Flop #(.trigger("falling")) j_k_ff_3 (
    .J(and_1_out), .clk(Clk), .K(decision_2_out_4), .Q(Qb), .Qn(j_k_ff_3_qn),
    .preset(load_identifier_2_preset), .en(Enable), .reset(load_identifier_2_clear));
  J_K_Flip_Flop #(.trigger("falling")) j_k_ff_4 (
    .J(decision_4_out_4), .clk(Clk), .K(Qd), .Q(Qa), .Qn(j_k_ff_4_qn), .preset(load_identifier_1_preset),
    .en(Enable), .reset(load_identifier_1_clear));
  Decision decision_3 (.D(Decision_for_Skip), .X(or_2_out), .Y(and_2_out), .out_4(decision_3_out_4));
  and and_2 (and_2_out, Qd, j_k_ff_4_qn);
  or or_2 (or_2_out, Qb, and_2_out);
  and and_3 (and_3_out, Qb, Qd);
  Decision decision_4 (.D(Decision_for_Skip), .X(and_3_out), .Y(and_4_out), .out_4(decision_4_out_4));
  and and_4 (and_4_out, Qc, and_3_out);

  // Notes on the sheet:
  //   2107005
endmodule

module Mod_60_counter (
  input  CLk,
  input  Decision_for_load,
  input  MSB,
  input  in_4,
  input  in_5,
  input  in_6,
  input  in_7,
  input  in_8,
  input  LSB,
  input  Enable,
  output MSB_2,
  output out_12,
  output out_13,
  output out_14,
  output out_15,
  output out_16,
  output LSB_2
);

  wire nor_1_out, or_1_out;

  nor nor_1 (nor_1_out, MSB_2, out_12, out_13);
  Mod_6_Counter mod_6_counter_1 (
    .Clk(or_1_out), .Decision(Decision_for_load), .MSB(MSB), .in_5(in_4), .LSB(in_5), .Enable(Enable),
    .Qa(MSB_2), .Qb(out_12), .Qc(out_13));
  or or_1 (or_1_out, LSB_2, out_16, out_15, out_14);
  BCD_Counter bcd_counter_1 (
    .Clk(CLk), .Decision_for_load(Decision_for_load), .MSB(in_6), .in_4(in_7), .in_5(in_8), .LSB(LSB),
    .Decision_for_Skip(nor_1_out), .Enable(Enable), .Qa(out_14), .Qb(out_15), .Qc(out_16), .Qd(LSB_2));

  // Notes on the sheet:
  //   2107005
endmodule

module Binary_to_BCD (
  input  MSB,
  input  in_2,
  input  in_3,
  input  LSB,
  output MSB_2,
  output out_6,
  output out_7,
  output out_8,
  output LSB_2
);

  wire and_4_out, and_5_out, not_1_out, not_2_out, not_3_out, or_1_out;

  and and_1 (MSB_2, MSB, or_1_out);
  and and_2 (out_6, MSB, not_2_out, not_1_out);
  or or_1 (or_1_out, in_2, in_3);
  and and_3 (out_7, in_2, not_3_out);
  not not_1 (not_1_out, in_3);
  not not_2 (not_2_out, in_2);
  or or_2 (out_8, and_4_out, and_5_out);
  and and_4 (and_4_out, in_2, MSB);
  and and_5 (and_5_out, in_3, not_3_out);
  not not_3 (not_3_out, MSB);

  assign LSB_2 = LSB;

  // Notes on the sheet:
  //   2107005
endmodule

module Mod_13_Counter (
  input  Clk,
  input  Decision_for_Load,
  input  MSB,
  input  in_4,
  input  in_5,
  input  LSB,
  input  Enable,
  output MSB_2,
  output out_9,
  output out_10,
  output LSB_2
);

  wire and_1_out, and_2_out, and_3_out, load_identifier_1_clear, load_identifier_1_preset,
       load_identifier_2_clear, load_identifier_2_preset, load_identifier_3_clear, load_identifier_3_preset,
       load_identifier_4_clear, load_identifier_4_preset, or_1_out, or_2_out;

  Load_Identifier load_identifier_1 (
    .Decision(Decision_for_Load), .Load(MSB), .Preset(load_identifier_1_preset),
    .Clear(load_identifier_1_clear));
  Load_Identifier load_identifier_2 (
    .Decision(Decision_for_Load), .Load(in_4), .Preset(load_identifier_2_preset),
    .Clear(load_identifier_2_clear));
  Load_Identifier load_identifier_3 (
    .Decision(Decision_for_Load), .Load(in_5), .Preset(load_identifier_3_preset),
    .Clear(load_identifier_3_clear));
  Load_Identifier load_identifier_4 (
    .Decision(Decision_for_Load), .Load(LSB), .Preset(load_identifier_4_preset),
    .Clear(load_identifier_4_clear));
  T_Flip_Flop #(.trigger("falling")) t_ff_1 (
    .clk(Clk), .T(1'b1), .Q(LSB_2), .preset(load_identifier_4_preset), .reset(load_identifier_4_clear),
    .en(Enable));  // open: Qn
  T_Flip_Flop #(.trigger("falling")) t_ff_2 (
    .clk(Clk), .T(LSB_2), .Q(out_10), .preset(load_identifier_3_preset), .reset(load_identifier_3_clear),
    .en(Enable));  // open: Qn
  and and_1 (and_1_out, out_10, LSB_2);
  T_Flip_Flop #(.trigger("falling")) t_ff_3 (
    .clk(Clk), .T(or_1_out), .Q(out_9), .preset(load_identifier_2_preset), .reset(load_identifier_2_clear),
    .en(Enable));  // open: Qn
  or or_1 (or_1_out, and_1_out, and_3_out);
  and and_2 (and_2_out, and_1_out, out_9);
  or or_2 (or_2_out, and_2_out, and_3_out);
  and and_3 (and_3_out, out_9, MSB_2);
  T_Flip_Flop #(.trigger("falling")) t_ff_4 (
    .clk(Clk), .T(or_2_out), .Q(MSB_2), .preset(load_identifier_1_preset), .reset(load_identifier_1_clear),
    .en(Enable));  // open: Qn

  // Notes on the sheet:
  //   2107005
endmodule

module Load_Identifier (
  input  Decision,
  input  Load,
  output Preset,
  output Clear
);

  wire not_1_out;

  not not_1 (not_1_out, Load);
  and and_1 (Preset, Decision, Load);
  and and_2 (Clear, Decision, not_1_out);

  // Notes on the sheet:
  //   2107005
endmodule

module BCD_to_Binary (
  input  C4,
  input  C3,
  input  C2,
  input  C1,
  input  C0,
  output MSB,
  output out_7,
  output out_8,
  output LSB
);

  wire and_1_out;

  and and_1 (and_1_out, C4, C1);
  or or_1 (MSB, C4, C3);
  xor xor_1 (out_8, C4, C1);
  or or_2 (out_7, C2, and_1_out);

  assign LSB = C0;

  // Notes on the sheet:
  //   2107005
endmodule

module bcdto7 (
  input  in_1,
  input  in_2,
  input  in_3,
  input  in_4,
  output out_5,
  output out_6,
  output out_7,
  output out_8,
  output out_9,
  output out_10,
  output out_11
);

  b b_1 (.A(in_1), .B(in_2), .C(in_3), .D(in_4), .out_5(out_6));
  c c_1 (.A(in_1), .B(in_2), .C(in_3), .D(in_4), .out_5(out_7));
  d d_1 (.A(in_1), .B(in_2), .C(in_3), .D(in_4), .out_5(out_8));
  e e_1 (.A(in_1), .B(in_2), .C(in_3), .D(in_4), .out_5(out_9));
  f f_1 (.A(in_1), .B(in_2), .C(in_3), .D(in_4), .out_5(out_10));
  g g_1 (.A(in_1), .B(in_2), .C(in_3), .D(in_4), .out_5(out_11));
  a a_1 (.A(in_1), .B(in_2), .C(in_3), .D(in_4), .out_5(out_5));
endmodule

module a (
  input  A,
  input  B,
  input  C,
  input  D,
  output out_5
);

  wire not_1_out, not_2_out, not_3_out, not_4_out, or_1_out, xnor_1_out;

  not not_1 (not_1_out, A);
  not not_2 (not_2_out, B);
  not not_3 (not_3_out, C);
  not not_4 (not_4_out, D);
  or or_1 (or_1_out, A, C);
  xnor xnor_1 (xnor_1_out, B, D);
  or or_2 (out_5, or_1_out, xnor_1_out);
endmodule

module b (
  input  A,
  input  B,
  input  C,
  input  D,
  output out_5
);

  wire not_1_out, not_2_out, not_3_out, not_4_out, xnor_1_out;

  not not_1 (not_1_out, A);
  not not_2 (not_2_out, B);
  not not_3 (not_3_out, C);
  not not_4 (not_4_out, D);
  xnor xnor_1 (xnor_1_out, C, D);
  or or_1 (out_5, not_2_out, xnor_1_out);
endmodule

module c (
  input  A,
  input  B,
  input  C,
  input  D,
  output out_5
);

  wire not_1_out, not_2_out, not_3_out, not_4_out, or_1_out;

  not not_1 (not_1_out, A);
  not not_2 (not_2_out, B);
  not not_3 (not_3_out, C);
  not not_4 (not_4_out, D);
  or or_1 (or_1_out, B, not_3_out);
  or or_2 (out_5, or_1_out, D);
endmodule

module d (
  input  A,
  input  B,
  input  C,
  input  D,
  output out_5
);

  wire and_1_out, and_2_out, and_3_out, and_4_out, not_1_out, not_2_out, not_3_out, not_4_out, or_1_out,
       or_2_out, or_3_out;

  not not_1 (not_1_out, A);
  not not_2 (not_2_out, B);
  not not_3 (not_3_out, C);
  not not_4 (not_4_out, D);
  and and_1 (and_1_out, not_2_out, not_4_out);
  and and_2 (and_2_out, not_2_out, C);
  and and_3 (and_3_out, C, not_4_out);
  and and_4 (and_4_out, B, not_3_out, D);
  or or_1 (or_1_out, A, and_1_out);
  or or_2 (or_2_out, and_3_out, and_4_out);
  or or_3 (or_3_out, or_1_out, and_2_out);
  or or_4 (out_5, or_3_out, or_2_out);
endmodule

module e (
  input  A,
  input  B,
  input  C,
  input  D,
  output out_5
);

  wire and_1_out, and_2_out, not_1_out, not_2_out, not_3_out, not_4_out;

  not not_1 (not_1_out, A);
  not not_2 (not_2_out, B);
  not not_3 (not_3_out, C);
  not not_4 (not_4_out, D);
  and and_1 (and_1_out, not_2_out, not_4_out);
  and and_2 (and_2_out, C, not_4_out);
  or or_1 (out_5, and_1_out, and_2_out);
endmodule

module f (
  input  A,
  input  B,
  input  C,
  input  D,
  output out_5
);

  wire and_1_out, and_2_out, and_3_out, not_1_out, not_2_out, not_3_out, not_4_out, or_1_out, or_2_out;

  not not_1 (not_1_out, A);
  not not_2 (not_2_out, B);
  not not_3 (not_3_out, C);
  not not_4 (not_4_out, D);
  and and_1 (and_1_out, B, not_3_out);
  and and_2 (and_2_out, B, not_4_out);
  and and_3 (and_3_out, not_3_out, not_4_out);
  or or_1 (or_1_out, A, and_1_out);
  or or_2 (or_2_out, and_2_out, and_3_out);
  or or_3 (out_5, or_1_out, or_2_out);
endmodule

module g (
  input  A,
  input  B,
  input  C,
  input  D,
  output out_5
);

  wire and_1_out, and_2_out, and_3_out, not_1_out, not_2_out, not_3_out, not_4_out, or_1_out, or_2_out;

  not not_1 (not_1_out, A);
  not not_2 (not_2_out, B);
  not not_3 (not_3_out, C);
  not not_4 (not_4_out, D);
  and and_1 (and_1_out, B, not_4_out);
  and and_2 (and_2_out, B, not_3_out);
  and and_3 (and_3_out, not_2_out, C);
  or or_1 (or_1_out, and_2_out, and_3_out);
  or or_2 (or_2_out, A, and_1_out);
  or or_3 (out_5, or_2_out, or_1_out);
endmodule
